// Logisim project Lab1.circ as structural Verilog: 7 circuits, main circuit main
module main (
  input  A0,
  input  A1,
  input  A2,
  input  A3,
  input  B0,
  input  B1,
  input  B2,
  input  B3,
  input  in_9,
  input  R_W_selector,
  input  in_11
);

  wire Adder_s0, Adder_s1, Adder_s2, Adder_s3, AND_out_9, AND_out_10, AND_out_11, AND_out_12, clock_1_out,
       DFF_2_out_4, DFF_3_out_4, DFF_4_out_4, DFF_5_out_4, DFF_6_out_4, DFF_7_out_4, DFF_8_out_4,
       DFF_9_out_4, DFF_10_out_4, DFF_11_out_4, DFF_12_out_4, DFF_out_4, MUX__C_out_19, MUX__C_out_20,
       MUX__C_out_21, MUX__C_out_22, OR_out_9, OR_out_10, OR_out_11, OR_out_12, Subtractor_s0, Subtractor_s1,
       Subtractor_s2, Subtractor_s3;

  Clock clock_1 (.out(clock_1_out));
  Adder Adder (
    .A0(A0), .B0(B0), .A1(A1), .B1(B1), .A2(A2), .B2(B2), .A3(A3), .B3(B3), .S0(Adder_s0), .S1(Adder_s1),
    .S2(Adder_s2), .S3(Adder_s3));  // open: C4
  subtractor Subtractor (
    .A0(A0), .B0(B0), .A1(A1), .B1(B1), .A2(A2), .B2(B2), .A3(A3), .B3(B3), .S0(Subtractor_s0),
    .S1(Subtractor_s1), .S2(Subtractor_s2), .S3(Subtractor_s3));  // open: C4
  AND AND (
    .A0(A0), .B0(B0), .A1(A1), .B1(B1), .A2(A2), .B2(B2), .A3(A3), .B3(B3), .out_9(AND_out_9),
    .out_10(AND_out_10), .out_11(AND_out_11), .out_12(AND_out_12));
  OR OR (
    .A0(A0), .B0(B0), .A1(A1), .B1(B1), .A2(A2), .B2(B2), .A3(A3), .B3(B3), .out_9(OR_out_9),
    .out_10(OR_out_10), .out_11(OR_out_11), .out_12(OR_out_12));
  _4_channel_4_bit_MUX MUX__C (
    ._1(Adder_s0), ._2(Adder_s1), ._3(Adder_s2), ._4(Adder_s3), ._5(Subtractor_s0), ._6(Subtractor_s1),
    ._7(Subtractor_s2), ._8(Subtractor_s3), ._9(AND_out_9), ._10(AND_out_10), ._11(AND_out_11),
    ._12(AND_out_12), ._13(OR_out_9), ._14(OR_out_10), ._15(OR_out_11), ._16(OR_out_12), .in_17(in_9),
    .in_18(R_W_selector), .out_19(MUX__C_out_19), .out_20(MUX__C_out_20), .out_21(MUX__C_out_21),
    .out_22(MUX__C_out_22));
  DFF DFF (.Selector(in_11), .Input(A0), .Clk(clock_1_out), .out_4(DFF_out_4));  // open: out_5
  DFF DFF_2 (.Selector(in_11), .Input(A1), .Clk(clock_1_out), .out_4(DFF_2_out_4));  // open: out_5
  DFF DFF_3 (.Selector(in_11), .Input(A2), .Clk(clock_1_out), .out_4(DFF_3_out_4));  // open: out_5
  DFF DFF_4 (.Selector(in_11), .Input(A3), .Clk(clock_1_out), .out_4(DFF_4_out_4));  // open: out_5
  DFF DFF_5 (.Selector(in_11), .Input(B0), .Clk(clock_1_out), .out_4(DFF_5_out_4));  // open: out_5
  DFF DFF_6 (.Selector(in_11), .Input(B1), .Clk(clock_1_out), .out_4(DFF_6_out_4));  // open: out_5
  DFF DFF_7 (.Selector(in_11), .Input(B2), .Clk(clock_1_out), .out_4(DFF_7_out_4));  // open: out_5
  DFF DFF_8 (.Selector(in_11), .Input(B3), .Clk(clock_1_out), .out_4(DFF_8_out_4));  // open: out_5
  DFF DFF_9 (.Selector(in_11), .Input(MUX__C_out_19), .Clk(clock_1_out), .out_4(DFF_9_out_4));  // open: out_5
  DFF DFF_10 (.Selector(in_11), .Input(MUX__C_out_20), .Clk(clock_1_out), .out_4(DFF_10_out_4));  // open: out_5
  DFF DFF_11 (.Selector(in_11), .Input(MUX__C_out_21), .Clk(clock_1_out), .out_4(DFF_11_out_4));  // open: out_5
  DFF DFF_12 (.Selector(in_11), .Input(MUX__C_out_22), .Clk(clock_1_out), .out_4(DFF_12_out_4));  // open: out_5
  LED led_1 (.in(DFF_out_4));
  LED led_2 (.in(DFF_2_out_4));
  LED led_3 (.in(DFF_3_out_4));
  LED led_4 (.in(DFF_4_out_4));
  LED led_5 (.in(DFF_5_out_4));
  LED led_6 (.in(DFF_6_out_4));
  LED led_7 (.in(DFF_7_out_4));
  LED led_8 (.in(DFF_8_out_4));
  LED led_9 (.in(DFF_9_out_4));
  LED led_10 (.in(DFF_10_out_4));
  LED led_11 (.in(DFF_11_out_4));
  LED led_12 (.in(DFF_12_out_4));

  // Notes on the sheet:
  //   arithmetic/logic selector
  //   add/subtract and and/or selector
  //   A
  //   B
  //   C
endmodule

module Adder (
  input  A0,
  input  B0,
  input  A1,
  input  B1,
  input  A2,
  input  B2,
  input  A3,
  input  B3,
  output S0,
  output S1,
  output S2,
  output S3,
  output C4
);

  wire and_1_out, and_2_out, and_3_out, and_4_out, and_5_out, and_6_out, and_7_out, and_8_out, or_1_out,
       or_2_out, or_3_out, xor_1_out, xor_2_out, xor_3_out, xor_4_out, xor_5_out, xor_6_out, xor_7_out,
       xor_8_out, xor_13_out;

  xor xor_1 (xor_1_out, B0, 1'b0);
  xor xor_2 (xor_2_out, B1, 1'b0);
  xor xor_3 (xor_3_out, B2, 1'b0);
  xor xor_4 (xor_4_out, B3, 1'b0);
  xor xor_5 (xor_5_out, A0, xor_1_out);
  and and_1 (and_1_out, A0, xor_1_out);
  xor xor_6 (xor_6_out, A1, xor_2_out);
  and and_2 (and_2_out, A1, xor_2_out);
  xor xor_7 (xor_7_out, A2, xor_3_out);
  and and_3 (and_3_out, A2, xor_3_out);
  xor xor_8 (xor_8_out, A3, xor_4_out);
  and and_4 (and_4_out, A3, xor_4_out);
  xor xor_9 (S0, xor_5_out, 1'b0);
  and and_5 (and_5_out, xor_5_out, 1'b0);
  xor xor_10 (S1, xor_6_out, or_1_out);
  and and_6 (and_6_out, xor_6_out, or_1_out);
  xor xor_11 (S2, xor_7_out, or_2_out);
  and and_7 (and_7_out, xor_7_out, or_2_out);
  xor xor_12 (S3, xor_8_out, or_3_out);
  and and_8 (and_8_out, xor_8_out, or_3_out);
  or or_1 (or_1_out, and_5_out, and_1_out);
  or or_2 (or_2_out, and_6_out, and_2_out);
  or or_3 (or_3_out, and_7_out, and_3_out);
  or or_4 (C4, and_8_out, and_4_out);
  xor xor_13 (xor_13_out, or_3_out, C4);
  LED led_1 (.in(xor_13_out));

  // Notes on the sheet:
  //   M
  //   Co
  //   C1
  //   C2
  //   C3
  //   C4
  //   V
endmodule

module subtractor (
  input  A0,
  input  B0,
  input  A1,
  input  B1,
  input  A2,
  input  B2,
  input  A3,
  input  B3,
  output S0,
  output S1,
  output S2,
  output S3,
  output C4
);

  wire and_1_out, and_2_out, and_3_out, and_4_out, and_5_out, and_6_out, and_7_out, and_8_out, or_1_out,
       or_2_out, or_3_out, xor_1_out, xor_2_out, xor_3_out, xor_4_out, xor_5_out, xor_6_out, xor_7_out,
       xor_8_out, xor_13_out;

  xor xor_1 (xor_1_out, B0, 1'b1);
  xor xor_2 (xor_2_out, B1, 1'b1);
  xor xor_3 (xor_3_out, B2, 1'b1);
  xor xor_4 (xor_4_out, B3, 1'b1);
  xor xor_5 (xor_5_out, A0, xor_1_out);
  and and_1 (and_1_out, A0, xor_1_out);
  xor xor_6 (xor_6_out, A1, xor_2_out);
  and and_2 (and_2_out, A1, xor_2_out);
  xor xor_7 (xor_7_out, A2, xor_3_out);
  and and_3 (and_3_out, A2, xor_3_out);
  xor xor_8 (xor_8_out, A3, xor_4_out);
  and and_4 (and_4_out, A3, xor_4_out);
  xor xor_9 (S0, xor_5_out, 1'b1);
  and and_5 (and_5_out, xor_5_out, 1'b1);
  xor xor_10 (S1, xor_6_out, or_1_out);
  and and_6 (and_6_out, xor_6_out, or_1_out);
  xor xor_11 (S2, xor_7_out, or_2_out);
  and and_7 (and_7_out, xor_7_out, or_2_out);
  xor xor_12 (S3, xor_8_out, or_3_out);
  and and_8 (and_8_out, xor_8_out, or_3_out);
  or or_1 (or_1_out, and_5_out, and_1_out);
  or or_2 (or_2_out, and_6_out, and_2_out);
  or or_3 (or_3_out, and_7_out, and_3_out);
  or or_4 (C4, and_8_out, and_4_out);
  xor xor_13 (xor_13_out, or_3_out, C4);
  LED led_1 (.in(xor_13_out));

  // Notes on the sheet:
  //   M
  //   Co
  //   C1
  //   C2
  //   C3
  //   C4
  //   V
endmodule

module AND (
  input  A0,
  input  B0,
  input  A1,
  input  B1,
  input  A2,
  input  B2,
  input  A3,
  input  B3,
  output out_9,
  output out_10,
  output out_11,
  output out_12
);

  and and_1 (out_9, A0, B0);
  and and_2 (out_10, A1, B1);
  and and_3 (out_11, A2, B2);
  and and_4 (out_12, A3, B3);
endmodule

module OR (
  input  A0,
  input  B0,
  input  A1,
  input  B1,
  input  A2,
  input  B2,
  input  A3,
  input  B3,
  output out_9,
  output out_10,
  output out_11,
  output out_12
);

  or or_1 (out_9, A0, B0);
  or or_2 (out_10, A1, B1);
  or or_3 (out_11, A2, B2);
  or or_4 (out_12, A3, B3);
endmodule

module _4_channel_4_bit_MUX (
  input  _1,
  input  _2,
  input  _3,
  input  _4,
  input  _5,
  input  _6,
  input  _7,
  input  _8,
  input  _9,
  input  _10,
  input  _11,
  input  _12,
  input  _13,
  input  _14,
  input  _15,
  input  _16,
  input  in_17,
  input  in_18,
  output out_19,
  output out_20,
  output out_21,
  output out_22
);

  wire and_1_out, and_2_out, and_3_out, and_4_out, and_5_out, and_6_out, and_7_out, and_8_out, and_9_out,
       and_10_out, and_11_out, and_12_out, and_13_out, and_14_out, and_15_out, and_16_out, not_1_out,
       not_2_out, not_3_out, not_4_out;

  not not_1 (not_1_out, in_17);
  not not_2 (not_2_out, in_18);
  not not_3 (not_3_out, not_1_out);
  not not_4 (not_4_out, not_2_out);
  and and_1 (and_1_out, _1, not_1_out, not_2_out);
  and and_2 (and_2_out, _2, not_1_out, not_2_out);
  and and_3 (and_3_out, _3, not_1_out, not_2_out);
  and and_4 (and_4_out, _4, not_1_out, not_2_out);
  and and_5 (and_5_out, _5, not_1_out, not_4_out);
  and and_6 (and_6_out, _6, not_1_out, not_4_out);
  and and_7 (and_7_out, _7, not_1_out, not_4_out);
  and and_8 (and_8_out, _8, not_1_out, not_4_out);
  and and_9 (and_9_out, _9, not_3_out, not_2_out);
  and and_10 (and_10_out, _10, not_3_out, not_2_out);
  and and_11 (and_11_out, _11, not_3_out, not_2_out);
  and and_12 (and_12_out, _12, not_3_out, not_2_out);
  and and_13 (and_13_out, _13, not_3_out, not_4_out);
  and and_14 (and_14_out, _14, not_3_out, not_4_out);
  and and_15 (and_15_out, _15, not_3_out, not_4_out);
  and and_16 (and_16_out, _16, not_3_out, not_4_out);
  or or_1 (out_19, and_1_out, and_5_out, and_9_out, and_13_out);
  or or_2 (out_20, and_2_out, and_6_out, and_10_out, and_14_out);
  or or_3 (out_21, and_3_out, and_7_out, and_11_out, and_15_out);
  or or_4 (out_22, and_4_out, and_8_out, and_12_out, and_16_out);
endmodule

module DFF (
  input  Selector,
  input  Input,
  input  Clk,
  output out_4,
  output out_5
);

  wire and_1_out, and_2_out, nand_1_out, nand_2_out, nand_3_out, nand_4_out, not_1_out, or_1_out;

  not not_1 (not_1_out, Selector);
  and and_1 (and_1_out, out_4, not_1_out);
  and and_2 (and_2_out, Input, Selector);
  or or_1 (or_1_out, and_1_out, and_2_out);
  nand nand_1 (nand_1_out, nand_4_out, nand_2_out);
  nand nand_2 (nand_2_out, nand_1_out, Clk);
  nand nand_3 (nand_3_out, nand_2_out, Clk, nand_4_out);
  nand nand_4 (nand_4_out, nand_3_out, or_1_out);
  nand nand_5 (out_4, nand_2_out, out_5);
  nand nand_6 (out_5, out_4, nand_3_out);
endmodule
